// Logisim project p1.circ as structural Verilog: 1 circuit, main circuit main
module main (
  input  X,
  input  Y,
  output Z
);

  wire transistor_2_out;

  Transistor #(.\type ("n")) transistor_1 (.in(1'b0), .out(Z), .gate(X));
  Transistor transistor_2 (.in(1'b1), .out(transistor_2_out), .gate(X));
  Transistor transistor_3 (.in(transistor_2_out), .out(Z), .gate(Y));
  Transistor #(.\type ("n")) transistor_4 (.in(1'b0), .out(Z), .gate(Y));

  // Notes on the sheet:
  //   VDD
  //   GND
  //   NOR GATE
  //   SIDDHART THAKUR
  //   1601CS46
  //   ~(X+Y)
endmodule
