// Logisim project p3.circ as structural Verilog: 1 circuit, main circuit main
module main (
  input  A,
  input  B,
  output OUTPUT
);

  wire transistor_1_out, transistor_3_out, transistor_5_out, transistor_8_out, transistor_9_out,
       transistor_12_out;

  Transistor transistor_1 (.in(1'b1), .out(transistor_1_out), .gate(A));
  Transistor #(.\type ("n")) transistor_2 (.in(1'b0), .out(transistor_1_out), .gate(A));
  Transistor transistor_3 (.in(1'b1), .out(transistor_3_out), .gate(B));
  Transistor #(.\type ("n")) transistor_4 (.in(1'b0), .out(transistor_3_out), .gate(B));
  Transistor transistor_5 (.in(1'b1), .out(transistor_5_out), .gate(transistor_1_out));
  Transistor transistor_6 (.in(transistor_5_out), .out(OUTPUT), .gate(B));
  Transistor #(.\type ("n")) transistor_7 (.in(transistor_8_out), .out(OUTPUT), .gate(A));
  Transistor #(.\type ("n")) transistor_8 (.in(1'b0), .out(transistor_8_out), .gate(B));
  Transistor transistor_9 (.in(1'b1), .out(transistor_9_out), .gate(A));
  Transistor transistor_10 (.in(transistor_9_out), .out(OUTPUT), .gate(transistor_3_out));
  Transistor #(.\type ("n")) transistor_11 (.in(transistor_12_out), .out(OUTPUT), .gate(transistor_1_out));
  Transistor #(.\type ("n")) transistor_12 (.in(1'b0), .out(transistor_12_out), .gate(transistor_3_out));

  // Notes on the sheet:
  //   INPUTS
  //   A XOR B
  //   1601CS46
  //   GND
  //   SIDDHARTH THAKUR
  //   VDD
  //   A.~B + ~A.B
endmodule
