// Logisim project p4.circ as structural Verilog: 1 circuit, main circuit main
module main (
  input  A,
  input  B,
  input  C,
  output OUTPUT
);

  wire transistor_1_out, transistor_4_out, transistor_5_out;

  Transistor transistor_1 (.in(1'b1), .out(transistor_1_out), .gate(B));
  Transistor transistor_2 (.in(1'b1), .out(transistor_1_out), .gate(A));
  Transistor #(.\type ("n")) transistor_3 (.in(transistor_4_out), .out(transistor_1_out), .gate(A));
  Transistor #(.\type ("n")) transistor_4 (.in(transistor_5_out), .out(transistor_4_out), .gate(B));
  Transistor #(.\type ("n")) transistor_5 (.in(1'b0), .out(transistor_5_out), .gate(C));
  Transistor transistor_6 (.in(1'b1), .out(transistor_1_out), .gate(C));
  Transistor transistor_7 (.in(1'b1), .out(OUTPUT), .gate(transistor_1_out));
  Transistor #(.\type ("n")) transistor_8 (.in(1'b0), .out(OUTPUT), .gate(transistor_1_out));

  // Notes on the sheet:
  //   VDD
  //   GND
  //   3-INPUT AND GATE
  //   VDD
  //   GND
  //   1601CS46
  //   A.B.C
  //   SIDDHARTH THAKUR
endmodule
