// Logisim project p5.circ as structural Verilog: 1 circuit, main circuit main
module main (
  input  A,
  input  B,
  input  C,
  input  D,
  output A_B_C_D
);

  wire transistor_1_out, transistor_4_out, transistor_5_out, transistor_6_out;

  Transistor #(.\type ("n")) transistor_1 (.in(1'b0), .out(transistor_1_out), .gate(A));
  Transistor #(.\type ("n")) transistor_2 (.in(1'b0), .out(transistor_1_out), .gate(B));
  Transistor #(.\type ("n")) transistor_3 (.in(1'b0), .out(transistor_1_out), .gate(C));
  Transistor transistor_4 (.in(1'b1), .out(transistor_4_out), .gate(A));
  Transistor transistor_5 (.in(transistor_4_out), .out(transistor_5_out), .gate(B));
  Transistor transistor_6 (.in(transistor_5_out), .out(transistor_6_out), .gate(C));
  Transistor transistor_7 (.in(transistor_6_out), .out(transistor_1_out), .gate(D));
  Transistor #(.\type ("n")) transistor_8 (.in(1'b0), .out(transistor_1_out), .gate(D));
  Transistor transistor_9 (.in(1'b1), .out(A_B_C_D), .gate(transistor_1_out));
  Transistor #(.\type ("n")) transistor_10 (.in(1'b0), .out(A_B_C_D), .gate(transistor_1_out));

  // Notes on the sheet:
  //   4-INPUTS
  //   4-INPUT OR GATE
  //   VDD
  //   GND
  //   NOT GATE
  //   SIDDHARTH THAKUR
  //   1601CS46
endmodule
