// Logisim project p2.circ as structural Verilog: 1 circuit, main circuit main
module main (
  input  [7:0] in_1,
  input  in_2,
  input  [7:0] in_3,
  input  in_4,
  input  [7:0] in_5,
  input  in_6,
  input  [7:0] in_7,
  input  in_8,
  input  [18:0] in_9,
  input  in_10,
  input  [1:0] in_11,
  output [7:0] out_12,
  output [7:0] out_13,
  output [7:0] out_14,
  output [7:0] out_15
);

  wire decoder_1_out0, decoder_1_out1, decoder_1_out2, decoder_1_out3, not_1_out, not_2_out, not_3_out,
       not_4_out;

  Decoder #(.select(2), .enable("false")) decoder_1 (
    .out0(decoder_1_out0), .out1(decoder_1_out1), .out2(decoder_1_out2), .out3(decoder_1_out3), .sel(in_11));
  assign out_15 = in_2 ? in_1 : 8'bz;  // Controlled_Buffer controlled_buffer_1
  assign out_14 = in_4 ? in_3 : 8'bz;  // Controlled_Buffer controlled_buffer_2
  assign out_13 = in_6 ? in_5 : 8'bz;  // Controlled_Buffer controlled_buffer_3
  assign out_12 = in_8 ? in_7 : 8'bz;  // Controlled_Buffer controlled_buffer_4
  not not_1 (not_1_out, in_2);
  not not_2 (not_2_out, in_4);
  not not_3 (not_3_out, in_6);
  RAM #(.addrWidth(19), .bus("asynch")) ram_1 (
    .addr(in_9), .data(out_12), .sel(decoder_1_out0), .ld(not_4_out), .clr(in_10));
  not not_4 (not_4_out, in_8);
  RAM #(.addrWidth(19), .bus("asynch")) ram_2 (
    .addr(in_9), .data(out_12), .sel(decoder_1_out1), .ld(not_4_out));  // open: clr
  RAM #(.addrWidth(19), .bus("asynch")) ram_3 (
    .addr(in_9), .data(out_12), .sel(decoder_1_out2), .ld(not_4_out));  // open: clr
  RAM #(.addrWidth(19), .bus("asynch")) ram_4 (
    .addr(in_9), .data(out_12), .sel(decoder_1_out3), .ld(not_4_out));  // open: clr
  RAM #(.addrWidth(19), .bus("asynch")) ram_5 (
    .addr(in_9), .data(out_13), .sel(decoder_1_out0), .ld(not_3_out), .clr(in_10));
  RAM #(.addrWidth(19), .bus("asynch")) ram_6 (
    .addr(in_9), .data(out_13), .sel(decoder_1_out1), .ld(not_3_out));  // open: clr
  RAM #(.addrWidth(19), .bus("asynch")) ram_7 (
    .addr(in_9), .data(out_13), .sel(decoder_1_out2), .ld(not_3_out));  // open: clr
  RAM #(.addrWidth(19), .bus("asynch")) ram_8 (
    .addr(in_9), .data(out_13), .sel(decoder_1_out3), .ld(not_3_out));  // open: clr
  RAM #(.addrWidth(19), .bus("asynch")) ram_9 (
    .addr(in_9), .data(out_14), .sel(decoder_1_out0), .ld(not_2_out), .clr(in_10));
  RAM #(.addrWidth(19), .bus("asynch")) ram_10 (
    .addr(in_9), .data(out_14), .sel(decoder_1_out1), .ld(not_2_out));  // open: clr
  RAM #(.addrWidth(19), .bus("asynch")) ram_11 (
    .addr(in_9), .data(out_14), .sel(decoder_1_out2), .ld(not_2_out));  // open: clr
  RAM #(.addrWidth(19), .bus("asynch")) ram_12 (
    .addr(in_9), .data(out_14), .sel(decoder_1_out3), .ld(not_2_out));  // open: clr
  RAM #(.addrWidth(19), .bus("asynch")) ram_13 (
    .addr(in_9), .data(out_15), .sel(decoder_1_out0), .ld(not_1_out), .clr(in_10));
  RAM #(.addrWidth(19), .bus("asynch")) ram_14 (
    .addr(in_9), .data(out_15), .sel(decoder_1_out1), .ld(not_1_out));  // open: clr
  RAM #(.addrWidth(19), .bus("asynch")) ram_15 (
    .addr(in_9), .data(out_15), .sel(decoder_1_out2), .ld(not_1_out));  // open: clr
  RAM #(.addrWidth(19), .bus("asynch")) ram_16 (
    .data(out_15), .sel(decoder_1_out3), .ld(not_1_out));  // open: addr, clr

  // Notes on the sheet:
  //                                      2M * 32 Memory using 16 512K * 8 memory chips 
endmodule
