// Logisim project p1.circ as structural Verilog: 1 circuit, main circuit main
module main (
  input  A,
  input  B,
  input  C,
  input  D,
  output out_5,
  output out_6,
  output out_7,
  output out_8
);

  Transistor transistor_1 (.in(1'b1), .out(out_5), .gate(A));
  Transistor transistor_2 (.in(out_5), .out(out_6), .gate(B));
  Transistor transistor_3 (.in(out_6), .out(out_7), .gate(C));
  Transistor transistor_4 (.in(out_7), .out(out_8), .gate(D));

  // Notes on the sheet:
  //   VDD
  //   1601CS46
  //   SIDDHARTH THAKUR
endmodule
