// Logisim project p3.circ as structural Verilog: 1 circuit, main circuit main
module main (
  input  A,
  input  B,
  input  C,
  input  D,
  input  E,
  output OUTPUT
);

  wire transistor_1_out, transistor_2_out, transistor_7_out, transistor_9_out;

  Transistor transistor_1 (.in(1'b1), .out(transistor_1_out), .gate(A));
  Transistor transistor_2 (.in(transistor_1_out), .out(transistor_2_out), .gate(C));
  Transistor transistor_3 (.in(1'b1), .out(transistor_1_out), .gate(B));
  Transistor transistor_4 (.in(transistor_1_out), .out(transistor_2_out), .gate(D));
  Transistor transistor_5 (.in(transistor_2_out), .out(OUTPUT), .gate(E));
  Transistor #(.\type ("n")) transistor_6 (.in(transistor_7_out), .out(OUTPUT), .gate(A));
  Transistor #(.\type ("n")) transistor_7 (.in(1'b0), .out(transistor_7_out), .gate(B));
  Transistor #(.\type ("n")) transistor_8 (.in(transistor_9_out), .out(OUTPUT), .gate(C));
  Transistor #(.\type ("n")) transistor_9 (.in(1'b0), .out(transistor_9_out), .gate(D));
  Transistor #(.\type ("n")) transistor_10 (.in(1'b0), .out(OUTPUT), .gate(E));

  // Notes on the sheet:
  //   1601CS46
  //   SIDDHARTH THAKUR
endmodule
