// Logisim project p1.circ as structural Verilog: 2 circuits, main circuit main
module main (
  input  x,
  input  y,
  input  z,
  output \output 
);

  wire not_1_out, not_2_out, not_3_out, or_1_out, or_2_out;

  not not_1 (not_1_out, y);
  or or_1 (or_1_out, x, not_1_out, z);
  not not_2 (not_2_out, x);
  or or_2 (or_2_out, not_2_out, y, not_3_out);
  not not_3 (not_3_out, z);
  and and_1 (\output , or_1_out, or_2_out);

  // Notes on the sheet:
  //   dog
  //   goat
  //   cabbage
  //   p1 (a)
  //   SIDDHARTH THAKUR (1601CS46)
endmodule

module p1_b (
  input  x,
  input  y,
  input  z,
  input  w,
  output \output 
);

  wire and_1_out, and_2_out, and_3_out, and_4_out, not_1_out, not_2_out, not_3_out, not_4_out, not_5_out,
       not_6_out;

  not not_1 (not_1_out, x);
  not not_2 (not_2_out, y);
  not not_3 (not_3_out, w);
  not not_4 (not_4_out, y);
  not not_5 (not_5_out, z);
  not not_6 (not_6_out, w);
  and and_1 (and_1_out, not_1_out, not_2_out, w);
  and and_2 (and_2_out, not_4_out, not_5_out, w);
  and and_3 (and_3_out, y, z, not_6_out);
  and and_4 (and_4_out, x, y, not_3_out);
  or or_1 (\output , and_1_out, and_2_out, and_3_out, and_4_out);

  // Notes on the sheet:
  //   dog
  //   goat
  //   cabbage
  //   farmer
  //   SIDDHARTH THAKUR
  //   1601CS46
  //   p1(b)
endmodule
