// Logisim project p3.circ as structural Verilog: 6 circuits, main circuit main
module main (
);


  // Notes on the sheet:
  //        please see left-pane
  //   ALL ANSWERS ARE IN SUB-CIRCUITS
endmodule

module p3_a (
  input  A,
  input  B,
  output Y
);

  wire and_1_out, and_2_out, and_3_out, not_1_out, not_2_out, not_3_out;

  not not_1 (not_1_out, A);
  and and_1 (and_1_out, not_1_out, not_2_out);
  not not_2 (not_2_out, B);
  and and_2 (and_2_out, A, not_3_out);
  not not_3 (not_3_out, B);
  and and_3 (and_3_out, A, B);
  or or_1 (Y, and_1_out, and_2_out, and_3_out);
endmodule

module p3_b (
  input  A,
  input  B,
  input  C,
  output Y
);

  wire and_1_out, and_2_out, not_1_out, not_2_out, not_3_out;

  not not_1 (not_1_out, A);
  not not_2 (not_2_out, B);
  and and_1 (and_1_out, not_1_out, not_2_out, not_3_out);
  not not_3 (not_3_out, C);
  and and_2 (and_2_out, A, B, C);
  or or_1 (Y, and_1_out, and_2_out);
endmodule

module p3_c (
  input  A,
  input  B,
  input  C,
  output Y
);

  wire and_1_out, and_2_out, and_3_out, and_4_out, and_5_out, not_1_out, not_2_out, not_3_out, not_4_out,
       not_5_out, not_6_out, not_7_out, not_8_out;

  not not_1 (not_1_out, A);
  not not_2 (not_2_out, B);
  and and_1 (and_1_out, not_1_out, not_2_out, not_3_out);
  not not_3 (not_3_out, C);
  not not_4 (not_4_out, A);
  and and_2 (and_2_out, not_4_out, B, not_5_out);
  not not_5 (not_5_out, C);
  and and_3 (and_3_out, A, not_6_out, not_7_out);
  not not_6 (not_6_out, B);
  not not_7 (not_7_out, C);
  not not_8 (not_8_out, B);
  and and_4 (and_4_out, A, not_8_out, C);
  and and_5 (and_5_out, A, B, C);
  or or_1 (Y, and_1_out, and_2_out, and_3_out, and_4_out, and_5_out);

  // Notes on the sheet:
  //   SIDDHARTH THAKUR (1601CS46)
  //   Y
endmodule

module p3_d (
  input  A,
  input  B,
  input  C,
  input  D,
  output Y
);

  wire and_1_out, and_2_out, and_3_out, and_4_out, and_5_out, and_6_out, and_7_out, not_1_out, not_2_out,
       not_3_out, not_4_out, not_5_out, not_6_out, not_7_out, not_8_out, not_9_out, not_10_out, not_11_out,
       not_12_out, not_13_out, not_14_out, not_15_out, not_16_out, not_17_out, not_18_out;

  not not_1 (not_1_out, A);
  not not_2 (not_2_out, B);
  not not_3 (not_3_out, C);
  not not_4 (not_4_out, D);
  not not_5 (not_5_out, B);
  not not_6 (not_6_out, B);
  not not_7 (not_7_out, B);
  not not_8 (not_8_out, C);
  not not_9 (not_9_out, D);
  and and_1 (and_1_out, not_1_out, not_2_out, not_3_out, not_4_out);
  not not_10 (not_10_out, A);
  and and_2 (and_2_out, not_10_out, not_5_out, not_11_out, D);
  not not_11 (not_11_out, C);
  not not_12 (not_12_out, A);
  and and_3 (and_3_out, not_12_out, not_6_out, C, not_13_out);
  not not_13 (not_13_out, D);
  not not_14 (not_14_out, A);
  and and_4 (and_4_out, not_14_out, not_7_out, C, D);
  not not_15 (not_15_out, B);
  and and_5 (and_5_out, A, not_15_out, not_8_out, not_9_out);
  not not_16 (not_16_out, B);
  and and_6 (and_6_out, A, not_16_out, C, not_17_out);
  not not_17 (not_17_out, D);
  and and_7 (and_7_out, A, B, C, not_18_out);
  not not_18 (not_18_out, D);
  or or_1 (Y, and_1_out, and_2_out, and_3_out, and_4_out, and_5_out, and_6_out, and_7_out);

  // Notes on the sheet:
  //   SIDDHARTH THAKUR
  //   1601CS46
endmodule

module p3_e (
  input  A,
  input  B,
  input  C,
  input  D,
  output Y
);

  wire and_1_out, and_2_out, and_3_out, and_4_out, and_5_out, and_6_out, and_7_out, and_8_out, not_1_out,
       not_2_out, not_3_out, not_4_out;

  not not_1 (not_1_out, A);
  not not_2 (not_2_out, B);
  not not_3 (not_3_out, C);
  not not_4 (not_4_out, D);
  and and_1 (and_1_out, not_1_out, not_2_out, not_3_out, not_4_out);
  and and_2 (and_2_out, not_1_out, not_2_out, C, D);
  and and_3 (and_3_out, not_1_out, B, not_3_out, D);
  and and_4 (and_4_out, not_1_out, B, C, not_4_out);
  and and_5 (and_5_out, A, not_2_out, not_3_out, D);
  and and_6 (and_6_out, A, not_2_out, C, not_4_out);
  and and_7 (and_7_out, A, B, not_3_out, not_4_out);
  and and_8 (and_8_out, A, B, C, D);
  or or_1 (Y, and_1_out, and_2_out, and_3_out, and_4_out, and_5_out, and_6_out, and_7_out, and_8_out);
endmodule
