// Logisim project p6.circ as structural Verilog: 2 circuits, main circuit p6
module main (
  input  X,
  input  Y,
  input  Z,
  input  W
);

  wire p6_1_a, p6_1_b, p6_1_c, p6_1_d, p6_1_e, p6_1_f, p6_1_g;

  p6 p6_1 (
    .X(X), .Y(Y), .Z(Z), .W(W), .a(p6_1_a), .b(p6_1_b), .c(p6_1_c), .d(p6_1_d), .e(p6_1_e), .f(p6_1_f),
    .g(p6_1_g));
  _7_Segment_Display u_7_segment_display_1 (
    .g(p6_1_g), .f(p6_1_f), .a(p6_1_a), .b(p6_1_b), .e(p6_1_e), .d(p6_1_d), .c(p6_1_c));  // open: dp
endmodule

module p6 (
  input  X,
  input  Y,
  input  Z,
  input  W,
  output a,
  output b,
  output c,
  output d,
  output e,
  output f,
  output g
);

  wire and_1_out, and_2_out, and_3_out, and_4_out, and_5_out, and_6_out, and_7_out, and_8_out, and_9_out,
       and_10_out, and_11_out, and_12_out, and_13_out, and_14_out, and_15_out, and_16_out, and_17_out,
       and_18_out, and_19_out, and_20_out, and_21_out, and_22_out, and_23_out, and_24_out, and_25_out,
       and_26_out, and_27_out, and_28_out, and_29_out, and_30_out, and_31_out, and_32_out, and_33_out,
       and_34_out, and_35_out, and_36_out, not_1_out, not_2_out, not_3_out, not_4_out, not_5_out, not_6_out,
       not_7_out, not_8_out, not_9_out, not_10_out, not_11_out, not_12_out, not_13_out, not_14_out,
       not_15_out, not_16_out, not_17_out, not_18_out, not_19_out, not_20_out, not_21_out, not_22_out,
       not_23_out, not_24_out, not_25_out, not_26_out, not_27_out, not_28_out, not_29_out, not_30_out,
       not_31_out, not_32_out, not_33_out, not_34_out, not_35_out, not_36_out, not_37_out, not_38_out,
       not_39_out, not_40_out, not_41_out, not_42_out, not_43_out, not_44_out, not_45_out, not_46_out,
       not_47_out, undriven;

  not not_1 (not_1_out, Y);
  not not_2 (not_2_out, W);
  not not_3 (not_3_out, X);
  not not_4 (not_4_out, X);
  not not_5 (not_5_out, Y);
  not not_6 (not_6_out, Z);
  not not_7 (not_7_out, W);
  not not_8 (not_8_out, X);
  not not_9 (not_9_out, Y);
  not not_10 (not_10_out, X);
  not not_11 (not_11_out, Z);
  not not_12 (not_12_out, W);
  not not_13 (not_13_out, Y);
  not not_14 (not_14_out, W);
  not not_15 (not_15_out, X);
  not not_16 (not_16_out, Z);
  not not_17 (not_17_out, X);
  not not_18 (not_18_out, Z);
  not not_19 (not_19_out, X);
  not not_20 (not_20_out, Z);
  not not_21 (not_21_out, X);
  not not_22 (not_22_out, Y);
  not not_23 (not_23_out, X);
  not not_24 (not_24_out, Y);
  not not_25 (not_25_out, W);
  not not_26 (not_26_out, Y);
  not not_27 (not_27_out, Z);
  not not_28 (not_28_out, W);
  not not_29 (not_29_out, Z);
  not not_30 (not_30_out, W);
  not not_31 (not_31_out, Y);
  not not_32 (not_32_out, W);
  not not_33 (not_33_out, W);
  not not_34 (not_34_out, Z);
  not not_35 (not_35_out, W);
  not not_36 (not_36_out, X);
  not not_37 (not_37_out, Z);
  not not_38 (not_38_out, W);
  not not_39 (not_39_out, Y);
  not not_40 (not_40_out, X);
  not not_41 (not_41_out, W);
  not not_42 (not_42_out, Y);
  not not_43 (not_43_out, W);
  not not_44 (not_44_out, Y);
  not not_45 (not_45_out, W);
  not not_46 (not_46_out, X);
  not not_47 (not_47_out, Z);
  and and_1 (and_1_out, not_1_out, not_2_out);
  and and_2 (and_2_out, not_3_out, Z);
  and and_3 (and_3_out, not_4_out, Y, W);
  and and_4 (and_4_out, Y, Z);
  and and_5 (and_5_out, X, not_5_out, not_6_out);
  and and_6 (and_6_out, X, not_7_out);
  and and_7 (and_7_out, not_8_out, not_9_out);
  and and_8 (and_8_out, not_10_out, not_11_out, not_12_out);
  and and_9 (and_9_out, not_13_out, not_14_out);
  and and_10 (and_10_out, not_15_out, Z, W);
  and and_11 (and_11_out, X, not_16_out, W);
  and and_12 (and_12_out, not_17_out, not_18_out);
  and and_13 (and_13_out, not_19_out, W);
  and and_14 (and_14_out, not_20_out, W);
  and and_15 (and_15_out, not_21_out, Y);
  and and_16 (and_16_out, X, not_22_out);
  and and_17 (and_17_out, not_23_out, not_24_out, not_25_out);
  and and_18 (and_18_out, not_26_out, Z, W);
  and and_19 (and_19_out, Y, not_27_out, W);
  and and_20 (and_20_out, Y, Z, not_28_out);
  and and_21 (and_21_out, X, not_29_out, not_30_out);
  and and_22 (and_22_out, not_31_out, not_32_out);
  and and_23 (and_23_out, Z, not_33_out);
  and and_24 (and_24_out, X, Z);
  and and_25 (and_25_out, X, Y);
  and and_26 (and_26_out, not_34_out, not_35_out);
  and and_27 (and_27_out, not_36_out, Y, not_37_out);
  and and_28 (and_28_out, Y, not_38_out);
  and and_29 (and_29_out, X, not_39_out);
  and and_30 (and_30_out, X, Z);
  and and_31 (and_31_out, not_40_out, not_41_out);
  and and_32 (and_32_out, not_42_out, not_43_out);
  and and_33 (and_33_out, not_44_out, Z);
  and and_34 (and_34_out, Z, not_45_out);
  and and_35 (and_35_out, not_46_out, Y, not_47_out);
  and and_36 (and_36_out, X, W);
  or or_1 (c, and_12_out, and_13_out, and_14_out, and_15_out, and_16_out);
  or or_2 (d, and_17_out, and_18_out, and_19_out, and_20_out, and_21_out);
  or or_3 (e, and_22_out, and_23_out, and_24_out, and_25_out);
  or or_4 (a, and_1_out, and_2_out, and_3_out, and_4_out, and_5_out, and_6_out);
  or or_5 (b, and_7_out, and_8_out, and_9_out, and_10_out, and_11_out);
  or or_6 (g, and_31_out, and_32_out, and_33_out, and_34_out, and_35_out, and_36_out);
  or or_7 (f, and_26_out, and_27_out, and_28_out, and_29_out, and_30_out);
  _7_Segment_Display u_7_segment_display_1 (.g(g), .f(f), .a(a), .b(b), .e(e), .d(d), .c(c), .dp(undriven));
endmodule
