// Logisim project p5.circ as structural Verilog: 2 circuits, main circuit main
module main (
  input  [3:0] A,
  input  [3:0] B,
  input  [3:0] S0,
  input  a3,
  input  b3,
  input  a2,
  input  b2,
  input  a1,
  input  b1,
  input  a0,
  input  b0,
  input  S0_2,
  output [3:0] OUTPUT,
  output c3,
  output c2,
  output c1,
  output c0
);

  wire [3:0] and_1_out, and_2_out, not_1_out;

  assign not_1_out = ~S0;  // NOT_Gate not_1, 4 bits wide
  assign and_1_out = A & not_1_out;  // AND_Gate and_1, 4 bits wide
  assign and_2_out = B & S0;  // AND_Gate and_2, 4 bits wide
  assign OUTPUT = and_1_out | and_2_out;  // OR_Gate or_1, 4 bits wide
  _2_to_1_multiplexer u_2_to_1_multiplexer_1 (.I0(a3), .I1(b3), .S0(S0_2), .Y(c3));
  _2_to_1_multiplexer u_2_to_1_multiplexer_2 (.I0(a2), .I1(b2), .S0(S0_2), .Y(c2));
  _2_to_1_multiplexer u_2_to_1_multiplexer_3 (.I0(a1), .I1(b1), .S0(S0_2), .Y(c1));
  _2_to_1_multiplexer u_2_to_1_multiplexer_4 (.I0(a0), .I1(b0), .S0(S0_2), .Y(c0));

  // Notes on the sheet:
  //   Both are same
  //   C
endmodule

module _2_to_1_multiplexer (
  input  I0,
  input  I1,
  input  S0,
  output Y
);

  wire and_1_out, and_2_out, not_1_out;

  not not_1 (not_1_out, S0);
  and and_1 (and_1_out, I0, not_1_out);
  and and_2 (and_2_out, I1, S0);
  or or_1 (Y, and_1_out, and_2_out);
endmodule
