// Logisim project Buffer.circ as structural Verilog: 1 circuit, main circuit main
module main (
  input  in_1,
  output out_2
);

  Transistor #(.\type ("n")) transistor_1 (.in(1'b1), .out(out_2), .gate(in_1));
  Transistor transistor_2 (.in(1'b0), .out(out_2), .gate(in_1));
endmodule
