// Logisim project p4.circ as structural Verilog: 1 circuit, main circuit main
module main (
  input  in_1,
  input  in_2,
  input  in_3,
  input  in_4,
  input  in_5,
  input  in_6,
  input  in_7,
  input  [1:0] in_8,
  output out_9,
  output out_10,
  output out_11,
  output out_12
);

  wire clock_1_out, multiplexer_1_out, multiplexer_2_out, multiplexer_3_out, multiplexer_4_out;

  Multiplexer #(.select(2)) multiplexer_1 (
    .in0(in_3), .in1(out_10), .in2(in_1), .in3(out_9), .out(multiplexer_1_out), .sel(in_8));  // open: en
  Multiplexer #(.select(2)) multiplexer_2 (
    .in0(in_4), .in1(out_11), .in2(out_9), .in3(out_10), .out(multiplexer_2_out), .sel(in_8));  // open: en
  Multiplexer #(.select(2)) multiplexer_3 (
    .in0(in_5), .in1(out_12), .in2(out_10), .in3(out_11), .out(multiplexer_3_out), .sel(in_8));  // open: en
  Multiplexer #(.select(2)) multiplexer_4 (
    .in0(in_6), .in1(in_7), .in2(out_11), .in3(out_12), .out(multiplexer_4_out), .sel(in_8));  // open: en
  Clock clock_1 (.out(clock_1_out));
  D_Flip_Flop d_ff_1 (.clk(clock_1_out), .D(multiplexer_1_out), .Q(out_9), .reset(in_2));  // open: Qn, preset, en
  D_Flip_Flop d_ff_2 (.clk(clock_1_out), .D(multiplexer_2_out), .Q(out_10), .reset(in_2));  // open: Qn, preset, en
  D_Flip_Flop d_ff_3 (.clk(clock_1_out), .D(multiplexer_3_out), .Q(out_11), .reset(in_2));  // open: Qn, preset, en
  D_Flip_Flop d_ff_4 (.clk(clock_1_out), .D(multiplexer_4_out), .Q(out_12), .reset(in_2));  // open: Qn, preset, en
  LED led_1 (.in(out_9));
  LED led_2 (.in(out_10));
  LED led_3 (.in(out_11));
  LED led_4 (.in(out_12));
endmodule
